// Logisim project 4bit_float.circ as structural Verilog: 3 circuits, main circuit main
module main (
  input  U3,
  input  U2,
  input  U1,
  input  U0,
  output F0,
  output F_1,
  output F_2,
  output F_3,
  output P1,
  output P0
);

  wire n74hc148_1_y0, n74hc148_1_y1, not_1_out, not_2_out, not_3_out;

  not not_1 (not_1_out, U3);
  not not_2 (not_2_out, U2);
  not not_3 (not_3_out, U1);
  not not_4 (P1, n74hc148_1_y1);
  _74HC148 u_74hc148_1 (
    .S(1'b0), .I0(1'b0), .I1(not_3_out), .I2(not_2_out), .I3(not_1_out), .I4(1'b1), .I5(1'b1), .I6(1'b1),
    .I7(1'b1), .Y0(n74hc148_1_y0), .Y1(n74hc148_1_y1));  // open: Y2, Yex, Ys
  not not_5 (P0, n74hc148_1_y0);
  _74HC153 u_74hc153_1 (
    .S1(1'b0), .D13(U3), .D12(U2), .D11(U1), .D10(U0), .S2(1'b0), .D23(U2), .D22(U1), .D21(U0), .D20(1'b0),
    .A1(P1), .A0(P0), .Y1(F0), .Y2(F_1));
  _74HC153 u_74hc153_2 (
    .S1(1'b0), .D13(U1), .D12(U0), .D11(1'b0), .D10(1'b0), .S2(1'b0), .D23(U0), .D22(1'b0), .D21(1'b0),
    .D20(1'b0), .A1(P1), .A0(P0), .Y1(F_2), .Y2(F_3));

  // Other names for the same wires on the sheet: A = P0; B = P1

  // Notes on the sheet:
  //   ·
endmodule

module _74HC148 (
  input  S,
  input  I0,
  input  I1,
  input  I2,
  input  I3,
  input  I4,
  input  I5,
  input  I6,
  input  I7,
  output Y0,
  output Y1,
  output Y2,
  output Yex,
  output Ys
);

  wire and_1_out, and_2_out, and_3_out, and_4_out, and_5_out, not_1_out, not_2_out, not_3_out, not_4_out,
       not_5_out, not_6_out, not_7_out, not_8_out, not_9_out, not_10_out, not_11_out, not_12_out, not_13_out,
       not_14_out, not_15_out, not_16_out, not_17_out, not_18_out, not_19_out, not_20_out, not_21_out,
       not_22_out, not_23_out, not_24_out, not_25_out, not_26_out, not_27_out, or_1_out, or_2_out, or_3_out,
       or_4_out;

  not not_1 (not_1_out, S);
  not not_2 (not_2_out, I0);
  not not_3 (not_3_out, I1);
  not not_4 (not_4_out, I2);
  not not_5 (not_5_out, I3);
  not not_6 (not_6_out, I4);
  not not_7 (not_7_out, I5);
  not not_8 (not_8_out, I6);
  not not_9 (not_9_out, I7);
  not not_10 (not_10_out, not_4_out);
  not not_11 (not_11_out, not_6_out);
  not not_12 (not_12_out, not_8_out);
  not not_13 (not_13_out, not_6_out);
  not not_14 (not_14_out, not_7_out);
  not not_15 (not_15_out, not_6_out);
  not not_16 (not_16_out, not_7_out);
  not not_17 (not_17_out, not_2_out);
  not not_18 (not_18_out, not_3_out);
  not not_19 (not_19_out, not_4_out);
  not not_20 (not_20_out, not_5_out);
  not not_21 (not_21_out, not_6_out);
  not not_22 (not_22_out, not_7_out);
  not not_23 (not_23_out, not_8_out);
  not not_24 (not_24_out, not_9_out);
  and and_1 (and_1_out, not_3_out, not_10_out, not_11_out, not_12_out);
  not not_25 (not_25_out, not_6_out);
  and and_2 (and_2_out, not_5_out, not_25_out, not_26_out);
  not not_26 (not_26_out, not_8_out);
  and and_3 (and_3_out, not_7_out, not_27_out);
  not not_27 (not_27_out, not_8_out);
  and and_4 (and_4_out, not_4_out, not_13_out, not_14_out);
  and and_5 (and_5_out, not_5_out, not_15_out, not_16_out);
  or or_1 (or_1_out, not_6_out, not_7_out, not_8_out, not_9_out);
  or or_2 (or_2_out, not_2_out, not_3_out, not_4_out, not_5_out, not_6_out, not_7_out, not_8_out, not_9_out);
  or or_3 (or_3_out, and_1_out, and_2_out, and_3_out, not_9_out);
  or or_4 (or_4_out, and_4_out, and_5_out, not_8_out, not_9_out);
  nand nand_1 (Y2, or_1_out, not_1_out);
  nand nand_2 (Yex, or_2_out, not_1_out);
  nand nand_3 (Ys, not_17_out, not_18_out, not_19_out, not_20_out, not_21_out, not_22_out, not_23_out, not_24_out, not_1_out);
  nand nand_4 (Y0, or_3_out, not_1_out);
  nand nand_5 (Y1, or_4_out, not_1_out);
endmodule

module _74HC153 (
  input  S1,
  input  D13,
  input  D12,
  input  D11,
  input  D10,
  input  S2,
  input  D23,
  input  D22,
  input  D21,
  input  D20,
  input  A1,
  input  A0,
  output Y1,
  output Y2
);

  wire and_1_out, and_2_out, and_3_out, and_4_out, and_5_out, and_6_out, and_7_out, and_8_out, not_1_out,
       not_2_out, not_3_out, not_4_out, not_5_out, not_6_out, not_7_out, not_8_out, not_9_out, not_10_out,
       or_1_out, or_2_out;

  not not_1 (not_1_out, S1);
  not not_2 (not_2_out, S2);
  not not_3 (not_3_out, A1);
  not not_4 (not_4_out, A0);
  and and_1 (and_1_out, not_3_out, not_4_out, D10);
  not not_5 (not_5_out, A1);
  and and_2 (and_2_out, not_5_out, A0, D11);
  and and_3 (and_3_out, A1, not_6_out, D12);
  not not_6 (not_6_out, A0);
  and and_4 (and_4_out, A1, A0, D13);
  not not_7 (not_7_out, A1);
  and and_5 (and_5_out, not_7_out, not_8_out, D20);
  not not_8 (not_8_out, A0);
  not not_9 (not_9_out, A1);
  and and_6 (and_6_out, not_9_out, A0, D21);
  not not_10 (not_10_out, A0);
  and and_7 (and_7_out, A1, not_10_out, D22);
  and and_8 (and_8_out, A1, A0, D23);
  or or_1 (or_1_out, and_1_out, and_2_out, and_3_out, and_4_out);
  or or_2 (or_2_out, and_5_out, and_6_out, and_7_out, and_8_out);
  and and_9 (Y1, or_1_out, not_1_out);
  and and_10 (Y2, or_2_out, not_2_out);
endmodule
